# Fritzing sketch Logger2 (saved by Fritzing 0.8.7b)

parts:
  パーツ1 = Arduino Wireless SD Shield
  パーツ2 = Arduino Uno (Rev3)  # not connected
  LED1 = LEDs [package=led10mm]
  BAT2 = Battery Holders [package=lipo-1100mAh]  # not connected

nets:
  N1: パーツ1.D8, LED1.C
  N2: パーツ1.GND, LED1.A

notes:
  シールドをスタック
  実際はDuemilanove
  実際にはEnergyShieldをスタックした
