# Fritzing sketch SensorLilypadv3_lipower (saved by Fritzing 0.8.7b)

parts:
  パーツ1 = LilyPad Temperature Sensor
  パーツ2 = LilyPad XBee
  パーツ4 = LilyPad LiPower
  U1 = LIPO-110mAh [package=lipo-110]  # not connected

nets:
  VCC: パーツ1.VCC, パーツ2.3.3V
  GND: パーツ1.GND, パーツ2.GND, パーツ4.GND
  N1: パーツ1.VO, パーツ2.D0
  N2: パーツ2.VCC, パーツ4.+

notes:
  温度センサ
  LiPo電池
  (容量はまちまち）
