# Fritzing sketch lilypad_Base19 (saved by Fritzing 0.8.7b)

parts:
  パーツ1 = Lilypad Arduino Board
  パーツ3 = LilyPad XBee
  パーツ16 = LilyPad LED
  パーツ19 = LilyPad LED
  パーツ14 = LilyPad LED
  パーツ20 = LilyPad LED  # not connected
  パーツ21 = LilyPad LED  # not connected
  パーツ22 = LilyPad LED
  パーツ23 = LilyPad LED
  パーツ24 = LilyPad Slide Switch
  パーツ25 = LilyPad Button Board
  パーツ26 = LilyPad LED  # not connected
  パーツ27 = LilyPad LED  # not connected
  パーツ28 = LilyPad LED  # not connected
  パーツ29 = LilyPad LED
  BAT1 = Battery Holders [package=lipo-1100mAh]

nets:
  GND: パーツ1.GND, パーツ3.GND, BAT1.-
  VCC: パーツ1.VCC, パーツ3.3.3V
  N1: パーツ1.D8, パーツ22.+
  N2: パーツ1.D9, パーツ23.+
  N3: パーツ1.D10, パーツ29.+
  N4: パーツ1.MOSI/D11, パーツ24.OFF
  N5: パーツ1.MISO/D12, パーツ25.S
  N6: パーツ1.D6, パーツ16.+
  N7: パーツ1.D5, パーツ14.+
  N8: パーツ1.D3, パーツ3.RX-I
  N9: パーツ1.D2, パーツ3.TX-O
  N10: パーツ1.D7, パーツ19.+
  N11: パーツ3.VCC, BAT1.+
  N12: パーツ16.-, パーツ19.-, パーツ14.-, パーツ22.-, パーツ23.-
  N13: パーツ24.ON, パーツ25.-

notes:
  XbeeとLilypadの接続は2，3番ピンにし、スケッチ側でソフトウェアシリアル対応
  2番　RX(Lilypad側がTx)
  3番　TX(Lilypad側がRx)
  それぞれのLEDは以下の意味
  5番　　緑　　　　　　　　　右翼優勢
  6番　　赤　　　　　　　　　左翼優勢
  7番　　黄　　　　　　　　　計測開始フラグ送信中
  8番　　白　　　　　　　　　優勢判定なし
  9番　　青　　　　　　　　　判定中
  10番　桃　　　　　　　　　信号バランス不安定
  11番　スライドスイッチ　　デバッグモード
  （OFFでデバッグモード）
  12番　プッシュスイッチ　　計測開始フラグ送信
  電源をLipo化するに当たり、LilyPadの変圧部品を加えた
